# Fritzing sketch qsoTrainer (saved by Fritzing 1.0.1rc)
circuit board: 10cm x 5cm
breadboards: 1

parts:
  Mod1 = Heltec WiFi Kit 8 [part_number=HTIT-W8266]
  R1 = Resistor [tolerance=±5% power=0.25 resistance=1k package=THT]
  U8 = AUDIO-JACK2 [package=audio-jack]
  RE1 = Rotary Encoder [package=THT]
  R2 = Rotary Potentiometer (Small) [maximum_resistance=10kΩ knob_status=50% power=0.5W package=THT]
  U9 = AUDIO-JACK2 [package=audio-jack]
  C1 = Electrolytic Capacitor [capacitance=10nF voltage=35V package="100 mil [THT, electrolytic]"]
  C2 = Electrolytic Capacitor [capacitance=10nF voltage=35V package="100 mil [THT, electrolytic]"]

nets:
  N1: Mod1.pin_2, RE1.SwitchrPinD
  N2: Mod1.pin_9, Mod1.pin_12, Mod1.pin_13, Mod1.pin_16, U8.SLEEVE, RE1.EncoderPinC, RE1.SwitchPinE, U9.SLEEVE, C1.-, C2.-
  N3: Mod1.pin_10, Mod1.pin_15
  N4: Mod1.pin_11, Mod1.pin_14
  N5: Mod1.pin_18, U9.RING, C1.+
  N6: Mod1.pin_19, R1.Pin_0
  N7: Mod1.pin_20, U9.TIP, C2.+
  N8: Mod1.pin_21, RE1.EncoderPinA
  N9: Mod1.pin_22, RE1.EncoderPinB
  N10: R1.Pin_1, R2.leg2
  N11: U8.RING, U8.TIP, R2.wiper

notes:
  morsetrainer by hb9fvk
  hb9fvk
  Headset
  Keyer
  Rotaryencoder
  Wifikit 8
  GPIO9 is GPIO0

custom parts:
  Heltec WiFi Kit 8: The Heltec WiFi Kit 8 is an IoT development board designed and produced by Heltec Automation and based on the Espressif ESP8266 processor module. The board includes built-in WiFi, a 0.91″ OLED display and a Li-Po battery management system. Links: Heltec WiFi Kit 8 product page Github
  Rotary Encoder: Rotary Encoder from ALPSec11e with switch.
